# Fritzing sketch Sketch_1_-_no_HW_debounce (saved by Fritzing 0.9.3b)
circuit board: 8.46667cm x 5.64444cm
breadboards: 1

parts:
  LED1 = LED - 3mm [color="Red (633nm)" package="3 mm [THT]"]
  R1 = Resistor [tolerance=±5% resistance=330 package=THT]
  LED2 = LED - 3mm [color="Green (560nm)" package="3 mm [THT]"]
  S1 = Momentary Switch [package=ksa_sealed_tac_switch]
  R2 = Resistor [tolerance=±5% resistance=330 package=THT]
  Raspberry_Pi1 = Raspberry Pi B+

nets:
  N1: LED1.cathode, R1.Pin_0
  N2: LED1.anode, Raspberry_Pi1.GPIO17
  N3: R1.Pin_1, S1.3, S1.4, R2.Pin_1, Raspberry_Pi1.GND
  N4: LED2.cathode, R2.Pin_0
  N5: LED2.anode, Raspberry_Pi1.GPIO27
  N6: S1.1, S1.2, Raspberry_Pi1.GPIO4
